// Logisim project Cravo_project.circ as structural Verilog: 18 circuits, main circuit ADD_4
module ADD_4 (
  input  [3:0] B,
  input  [3:0] A,
  input  CarryIN,
  output CarryOUT,
  output [3:0] S
);

  wire add_1_2_carryout, add_1_3_carryout, add_1_4_carryout;

  ADD_1 add_1_1 (.A(A[3]), .B(B[3]), .CarryIN(add_1_2_carryout), .S(S[3]), .CarryOUT(CarryOUT));
  ADD_1 add_1_2 (.A(A[2]), .B(B[2]), .CarryIN(add_1_3_carryout), .S(S[2]), .CarryOUT(add_1_2_carryout));
  ADD_1 add_1_3 (.A(A[1]), .B(B[1]), .CarryIN(add_1_4_carryout), .S(S[1]), .CarryOUT(add_1_3_carryout));
  ADD_1 add_1_4 (.A(A[0]), .B(B[0]), .CarryIN(CarryIN), .S(S[0]), .CarryOUT(add_1_4_carryout));
endmodule

module ADD_1 (
  input  A,
  input  B,
  input  CarryIN,
  output S,
  output CarryOUT
);

  wire and_1_out, and_2_out, or_1_out, xor_1_out;

  xor xor_1 (xor_1_out, A, B);
  or or_1 (or_1_out, CarryIN, B);
  and and_1 (and_1_out, CarryIN, B);
  LED led_1 (.in(S));
  xor xor_2 (S, xor_1_out, CarryIN);
  and and_2 (and_2_out, or_1_out, A);
  LED led_2 (.in(CarryOUT));
  or or_2 (CarryOUT, and_2_out, and_1_out);
endmodule

module BRAZIL (
  input  D,
  input  [3:0] A,
  input  [3:0] B,
  input  [2:0] \Operações ,
  output out_5,
  output [3:0] S,
  output ZERO
);

  wire add_4_1_carryout, decod_3x8_1_s0, decod_3x8_1_s1, decod_3x8_1_s2, decod_3x8_1_s3, decod_3x8_1_s4,
       decod_3x8_1_s5, decod_3x8_1_s6, decod_3x8_1_s7, sub_4_1_carryout;
  wire [3:0] add_4_1_s, buf_5_s, or_1_out_3, rot_l_1_abcd_2, rot_r_1_abcd_2, sub_4_1_s;

  OVERFLOW overflow_1 (
    .out_5(out_5), .in_1(sub_4_1_carryout), .in_2(decod_3x8_1_s2), .in_3(add_4_1_carryout),
    .in_4(decod_3x8_1_s1));
  DECOD_3X8 decod_3x8_1 (
    .OP(\Operações ), .S0(decod_3x8_1_s0), .S1(decod_3x8_1_s1), .S2(decod_3x8_1_s2), .S3(decod_3x8_1_s3),
    .S4(decod_3x8_1_s4), .S5(decod_3x8_1_s5), .S6(decod_3x8_1_s6), .S7(decod_3x8_1_s7));
  nor nor_1 (ZERO, decod_3x8_1_s7, decod_3x8_1_s6, S[0], S[1], S[2], S[3]);
  BUF buf_1 (.B(B), .in_2(decod_3x8_1_s0), .S(S));
  ADD_4 add_4_1 (.CarryOUT(add_4_1_carryout), .CarryIN(1'b0), .S(add_4_1_s), .A(A), .B(B));
  BUF buf_2 (.B(add_4_1_s), .in_2(decod_3x8_1_s1), .S(S));
  SUB_4 sub_4_1 (.B(B), .A(A), .CarryOUT(sub_4_1_carryout), .CarryIN(1'b0), .S(sub_4_1_s));
  BUF buf_3 (.B(sub_4_1_s), .in_2(decod_3x8_1_s2), .S(S));
  BUF buf_4 (.B(or_1_out_3), .in_2(decod_3x8_1_s3), .S(S));
  OR or_1 (.out_3(or_1_out_3), .A(A), .in_2(B));
  DEBUF debuf_1 (.B(B), .in_2(decod_3x8_1_s4), .S(S));
  ROT_L rot_l_1 (.ABCD(A), .XY(B[1:0]), .abcd_2(rot_l_1_abcd_2));
  BUF buf_5 (.B(rot_l_1_abcd_2), .in_2(D), .S(buf_5_s));
  ROT_R rot_r_1 (.ABCD(A), .XY(B[1:0]), .abcd_2(rot_r_1_abcd_2));
  BUF buf_6 (.B(rot_r_1_abcd_2), .in_2(D), .S(buf_5_s));
  BUF buf_7 (.B(buf_5_s), .in_2(decod_3x8_1_s5), .S(S));
endmodule

module SUB_1 (
  input  A,
  input  B,
  input  CarryIN,
  output S,
  output CarryOUT
);

  wire and_1_out, and_2_out, or_1_out, xor_1_out;

  xor xor_1 (xor_1_out, A, B);
  or or_1 (or_1_out, CarryIN, B);
  and and_1 (and_1_out, or_1_out, ~A);  // AND_Gate
  and and_2 (and_2_out, CarryIN, B);
  LED led_1 (.in(S));
  xor xor_2 (S, xor_1_out, CarryIN);
  LED led_2 (.in(CarryOUT));
  or or_2 (CarryOUT, and_1_out, and_2_out);
endmodule

module SUB_4 (
  input  [3:0] B,
  input  [3:0] A,
  input  CarryIN,
  output CarryOUT,
  output [3:0] S
);

  wire sub_1_2_carryout, sub_1_3_carryout, sub_1_4_carryout;

  SUB_1 sub_1_1 (.A(A[3]), .B(B[3]), .CarryIN(sub_1_2_carryout), .S(S[3]), .CarryOUT(CarryOUT));
  SUB_1 sub_1_2 (.A(A[2]), .B(B[2]), .CarryIN(sub_1_3_carryout), .S(S[2]), .CarryOUT(sub_1_2_carryout));
  SUB_1 sub_1_3 (.A(A[1]), .B(B[1]), .CarryIN(sub_1_4_carryout), .S(S[1]), .CarryOUT(sub_1_3_carryout));
  SUB_1 sub_1_4 (.A(A[0]), .B(B[0]), .CarryIN(CarryIN), .S(S[0]), .CarryOUT(sub_1_4_carryout));
endmodule

module BUF (
  input  [3:0] B,
  input  in_2,
  output [3:0] S
);

  assign S[3] = in_2 ? B[3] : 1'bz;  // Controlled_Buffer controlled_buffer_1
  assign S[1] = in_2 ? B[1] : 1'bz;  // Controlled_Buffer controlled_buffer_2
  assign S[2] = in_2 ? B[2] : 1'bz;  // Controlled_Buffer controlled_buffer_3
  assign S[0] = in_2 ? B[0] : 1'bz;  // Controlled_Buffer controlled_buffer_4
endmodule

module DEBUF (
  input  [3:0] B,
  input  in_2,
  output [3:0] S
);

  assign S[1] = in_2 ? ~B[1] : 1'bz;  // Controlled_Inverter controlled_inverter_1
  assign S[3] = in_2 ? ~B[3] : 1'bz;  // Controlled_Inverter controlled_inverter_2
  assign S[2] = in_2 ? ~B[2] : 1'bz;  // Controlled_Inverter controlled_inverter_3
  assign S[0] = in_2 ? ~B[0] : 1'bz;  // Controlled_Inverter controlled_inverter_4
endmodule

module DECOD_3X8 (
  input  [2:0] OP,
  output S0,
  output S1,
  output S2,
  output S3,
  output S4,
  output S5,
  output S6,
  output S7
);

  and and_1 (S0, ~OP[2], ~OP[1], ~OP[0]);  // AND_Gate
  and and_2 (S1, ~OP[2], ~OP[1], OP[0]);  // AND_Gate
  and and_3 (S2, ~OP[2], OP[1], ~OP[0]);  // AND_Gate
  and and_4 (S3, ~OP[2], OP[1], OP[0]);  // AND_Gate
  and and_5 (S4, OP[2], ~OP[1], ~OP[0]);  // AND_Gate
  and and_6 (S5, OP[2], ~OP[1], OP[0]);  // AND_Gate
  and and_7 (S6, OP[2], OP[1], ~OP[0]);  // AND_Gate
  and and_8 (S7, OP[2], OP[1], OP[0]);
endmodule

module ROT_L (
  input  [3:0] ABCD,
  input  [1:0] XY,
  output [3:0] abcd_2
);

  wire and_1_out, and_2_out, and_3_out, and_4_out, and_5_out, and_6_out, and_7_out, and_8_out, and_9_out;

  and and_1 (and_1_out, ~XY[1], ~XY[0], ABCD[3]);  // AND_Gate
  and and_2 (and_2_out, ~XY[1], XY[0], ABCD[2]);  // AND_Gate
  or or_1 (abcd_2[3], and_1_out, and_2_out, and_3_out, and_4_out);
  and and_3 (and_3_out, XY[1], ~XY[0], ABCD[1]);  // AND_Gate
  and and_4 (and_4_out, XY[1], XY[0], ABCD[0]);
  and and_5 (and_5_out, ~XY[1], ~XY[0], ABCD[2]);  // AND_Gate
  and and_6 (and_6_out, ~XY[1], XY[0], ABCD[1]);  // AND_Gate
  or or_2 (abcd_2[2], and_5_out, and_6_out, and_7_out);
  and and_7 (and_7_out, XY[1], ~XY[0], ABCD[0]);  // AND_Gate
  and and_8 (and_8_out, ~XY[1], ~XY[0], ABCD[1]);  // AND_Gate
  or or_3 (abcd_2[1], and_8_out, and_9_out);
  and and_9 (and_9_out, ~XY[1], XY[0], ABCD[0]);  // AND_Gate
  and and_10 (abcd_2[0], ~XY[1], ~XY[0], ABCD[0]);  // AND_Gate
endmodule

module ROT_R (
  input  [3:0] ABCD,
  input  [1:0] XY,
  output [3:0] abcd_2
);

  wire and_1_out, and_2_out, and_3_out, and_4_out, and_5_out, and_6_out, and_7_out, and_8_out, and_9_out;

  and and_1 (and_1_out, ~XY[1], ~XY[0], ABCD[0]);  // AND_Gate
  and and_2 (and_2_out, ~XY[1], XY[0], ABCD[1]);  // AND_Gate
  or or_1 (abcd_2[0], and_1_out, and_2_out, and_3_out, and_4_out);
  and and_3 (and_3_out, XY[1], ~XY[0], ABCD[2]);  // AND_Gate
  and and_4 (and_4_out, XY[1], XY[0], ABCD[3]);
  and and_5 (and_5_out, ~XY[1], ~XY[0], ABCD[1]);  // AND_Gate
  and and_6 (and_6_out, ~XY[1], XY[0], ABCD[2]);  // AND_Gate
  or or_2 (abcd_2[1], and_5_out, and_6_out, and_7_out);
  and and_7 (and_7_out, XY[1], ~XY[0], ABCD[3]);  // AND_Gate
  and and_8 (and_8_out, ~XY[1], ~XY[0], ABCD[2]);  // AND_Gate
  or or_3 (abcd_2[2], and_8_out, and_9_out);
  and and_9 (and_9_out, ~XY[1], XY[0], ABCD[3]);  // AND_Gate
  and and_10 (abcd_2[3], ~XY[1], ~XY[0], ABCD[3]);  // AND_Gate
endmodule

module OR (
  input  [3:0] A,
  input  [3:0] in_2,
  output [3:0] out_3
);

  or or_1 (out_3[3], A[3], in_2[3]);
  or or_2 (out_3[2], A[2], in_2[2]);
  or or_3 (out_3[1], A[1], in_2[1]);
  or or_4 (out_3[0], A[0], in_2[0]);
endmodule

module Main (
);

  wire brazil_1_out_5, brazil_1_zero, button_1_out, CLOCK_out, not_1_out, not_2_out, OVERFLOW_q,
       unid_ctrl_1_clk_ac, unid_ctrl_1_clk_ir, unid_ctrl_1_clk_pc, unid_ctrl_1_clk_ram,
       \unid_ctrl_1_direção , unid_ctrl_1_e, unid_ctrl_1_load, unid_ctrl_1_r_w, unid_ctrl_1_rst_pc, ZERO_q;
  wire [2:0] unid_ctrl_1_op;
  wire [3:0] brazil_1_s, counter_1_q, mux_1_s, ram_1_data, reg_ac_1_q, unid_ctrl_1_b_end, unid_ctrl_1_dados,
       unid_ctrl_1_operando;
  wire [7:0] ir_1_q, rom_1_data;

  not not_1 (not_1_out, unid_ctrl_1_load);
  Clock CLOCK (.out(CLOCK_out));
  ROM #(.addrWidth(4)) rom_1 (.addr(counter_1_q), .data(rom_1_data));  // open: sel
  IR ir_1 (.CLOCK(unid_ctrl_1_clk_ir), .D(rom_1_data), .Q(ir_1_q));
  Counter #(.width(4), .max('hf), .trigger("falling")) counter_1 (
    .load(unid_ctrl_1_load), .D(unid_ctrl_1_dados), .count(not_1_out), .Q(counter_1_q),
    .clk(unid_ctrl_1_clk_pc), .clr(unid_ctrl_1_rst_pc));  // open: carry
  // Probe on ir_1_q
  UNID_CTRL unid_ctrl_1 (
    .B_END(unid_ctrl_1_b_end), .OPERANDO(unid_ctrl_1_operando), .\DIREÇÃO (\unid_ctrl_1_direção ),
    .E(unid_ctrl_1_e), .OP(unid_ctrl_1_op), .\INSTRUÇÃO (ir_1_q), .CLOCK(CLOCK_out),
    .RST_PC(unid_ctrl_1_rst_pc), .RESET(button_1_out), .CLK_IR(unid_ctrl_1_clk_ir),
    .CLK_PC(unid_ctrl_1_clk_pc), .CLK_AC(unid_ctrl_1_clk_ac), .CLK_RAM(unid_ctrl_1_clk_ram),
    .DADOS(unid_ctrl_1_dados), .R_W(unid_ctrl_1_r_w), .LOAD(unid_ctrl_1_load), .ZERO(ZERO_q),
    .OVER(OVERFLOW_q));
  Button button_1 (.out(button_1_out));
  MUX mux_1 (.Controle(unid_ctrl_1_e), .E(unid_ctrl_1_operando), .D(ram_1_data), .S(mux_1_s));
  // Probe on mux_1_s
  // Probe on reg_ac_1_q
  BRAZIL brazil_1 (
    .A(reg_ac_1_q), .B(mux_1_s), .\Operações (unid_ctrl_1_op), .S(brazil_1_s), .D(\unid_ctrl_1_direção ),
    .out_5(brazil_1_out_5), .ZERO(brazil_1_zero));
  // Probe on brazil_1_s
  REG_AC reg_ac_1 (.CLOCK(unid_ctrl_1_clk_ac), .D(brazil_1_s), .Q(reg_ac_1_q));
  D_Flip_Flop OVERFLOW (.clk(unid_ctrl_1_clk_ac), .D(brazil_1_out_5), .Q(OVERFLOW_q));  // open: Qn, preset, en, reset
  D_Flip_Flop ZERO (.clk(unid_ctrl_1_clk_ac), .D(brazil_1_zero), .Q(ZERO_q));  // open: Qn, preset, en, reset
  RAM #(.addrWidth(4), .dataWidth(4)) ram_1 (
    .addr(unid_ctrl_1_b_end), .data(ram_1_data), .clk(unid_ctrl_1_clk_ram), .ld(unid_ctrl_1_r_w));  // open: sel, clr
  not not_2 (not_2_out, unid_ctrl_1_r_w);
  BUF_INV buf_inv_1 (.in_2(not_2_out), .in_1(reg_ac_1_q), .out_3(ram_1_data));

  // Notes on the sheet:
  //   contents of rom_1 (hex, n*v repeats v):
  //   0 f0 1 f1 10 31 d0 f2 11 f0 12 f1 e4
endmodule

module OVERFLOW (
  input  in_1,
  input  in_2,
  input  in_3,
  input  in_4,
  output out_5
);

  wire and_1_out, and_2_out;

  and and_1 (and_1_out, in_1, in_2);
  or or_1 (out_5, and_1_out, and_2_out);
  and and_2 (and_2_out, in_3, in_4);
endmodule

module REG_AC (
  input  CLOCK,
  input  [3:0] D,
  output [3:0] Q
);

  D_Flip_Flop d_ff_1 (.clk(CLOCK), .D(D[3]), .Q(Q[3]));  // open: Qn, preset, en, reset
  D_Flip_Flop d_ff_2 (.clk(CLOCK), .D(D[2]), .Q(Q[2]));  // open: Qn, preset, en, reset
  D_Flip_Flop d_ff_3 (.clk(CLOCK), .D(D[1]), .Q(Q[1]));  // open: Qn, preset, en, reset
  D_Flip_Flop d_ff_4 (.clk(CLOCK), .D(D[0]), .Q(Q[0]));  // open: Qn, preset, en, reset
endmodule

module MUX (
  input  [3:0] E,
  input  [3:0] D,
  input  Controle,
  output [3:0] S
);

  wire not_1_out;

  not not_1 (not_1_out, Controle);
  BUF buf_1 (.B(E), .in_2(not_1_out), .S(S));
  BUF buf_2 (.B(D), .in_2(Controle), .S(S));
endmodule

module BUF_INV (
  input  [3:0] in_1,
  input  in_2,
  output [3:0] out_3
);

  BUF buf_1 (.B(in_1), .in_2(in_2), .S(out_3));
endmodule

module IR (
  input  CLOCK,
  input  [7:0] D,
  output [7:0] Q
);

  D_Flip_Flop #(.trigger("falling")) D3 (.clk(CLOCK), .D(D[7]), .Q(Q[7]));  // open: Qn, preset, en, reset
  D_Flip_Flop #(.trigger("falling")) D2 (.clk(CLOCK), .D(D[6]), .Q(Q[6]));  // open: Qn, preset, en, reset
  D_Flip_Flop #(.trigger("falling")) D1 (.clk(CLOCK), .D(D[5]), .Q(Q[5]));  // open: Qn, preset, en, reset
  D_Flip_Flop #(.trigger("falling")) D0 (.clk(CLOCK), .D(D[4]), .Q(Q[4]));  // open: Qn, preset, en, reset
  D_Flip_Flop #(.trigger("falling")) D3_2 (.clk(CLOCK), .D(D[3]), .Q(Q[3]));  // open: Qn, preset, en, reset
  D_Flip_Flop #(.trigger("falling")) D2_2 (.clk(CLOCK), .D(D[2]), .Q(Q[2]));  // open: Qn, preset, en, reset
  D_Flip_Flop #(.trigger("falling")) D1_2 (.clk(CLOCK), .D(D[1]), .Q(Q[1]));  // open: Qn, preset, en, reset
  D_Flip_Flop #(.trigger("falling")) D0_2 (.clk(CLOCK), .D(D[0]), .Q(Q[0]));  // open: Qn, preset, en, reset
endmodule

module UNID_CTRL (
  input  CLOCK,
  input  [7:0] \INSTRUÇÃO ,
  input  RESET,
  input  OVER,
  input  ZERO,
  output [3:0] DADOS,
  output CLK_IR,
  output CLK_RAM,
  output [3:0] B_END,
  output RST_PC,
  output CLK_PC,
  output CLK_AC,
  output [3:0] OPERANDO,
  output \DIREÇÃO ,
  output E,
  output [2:0] OP,
  output R_W,
  output LOAD
);

  wire GOTO_out, JPO_out, JPZ_out, nand_1_out;
  wire [1:0] counter_1_q;

  Counter #(.width(2), .max('h3)) counter_1 (.Q(counter_1_q), .clk(CLOCK), .clr(RESET));  // open: load, D, count, carry
  nand STORAGE (R_W, CLK_AC, \INSTRUÇÃO [7], \INSTRUÇÃO [6], \INSTRUÇÃO [5], \INSTRUÇÃO [4]);
  and and_1 (CLK_IR, ~counter_1_q[0], ~counter_1_q[1]);  // AND_Gate
  and GOTO (GOTO_out, \INSTRUÇÃO [7], \INSTRUÇÃO [6], \INSTRUÇÃO [5], ~\INSTRUÇÃO [4], CLK_PC);  // AND_Gate
  and and_2 (CLK_PC, counter_1_q[0], ~counter_1_q[1]);  // AND_Gate
  and JPO (JPO_out, \INSTRUÇÃO [7], \INSTRUÇÃO [6], ~\INSTRUÇÃO [5], \INSTRUÇÃO [4], CLK_PC, OVER);  // AND_Gate
  or or_1 (LOAD, GOTO_out, JPO_out, JPZ_out);
  and and_3 (CLK_AC, ~counter_1_q[0], counter_1_q[1]);  // AND_Gate
  and and_4 (CLK_RAM, counter_1_q[0], counter_1_q[1]);
  and JPZ (JPZ_out, \INSTRUÇÃO [7], \INSTRUÇÃO [6], ~\INSTRUÇÃO [5], ~\INSTRUÇÃO [4], CLK_PC, ZERO);  // AND_Gate
  nand nand_1 (nand_1_out, \INSTRUÇÃO [7], ~\INSTRUÇÃO [6], \INSTRUÇÃO [5]);  // NAND_Gate
  and and_5 (E, \INSTRUÇÃO [4], nand_1_out);

  assign B_END = \INSTRUÇÃO [3:0];
  assign DADOS = \INSTRUÇÃO [3:0];
  assign \DIREÇÃO  = \INSTRUÇÃO [4];
  assign OP = \INSTRUÇÃO [7:5];
  assign OPERANDO = \INSTRUÇÃO [3:0];
  assign RST_PC = RESET;
endmodule
